# Fritzing sketch water_controller_schematics (saved by Fritzing 0.9.1b)

parts:
  Raspberry_Pi1 = Raspberry Pi B+
  U1 = RELAY-SOLIDSTATE [package=relay-s108t02]
  U2 = RELAY-SOLIDSTATE [package=relay-s108t02]
  proto1 = Adafruit_PermaProto_1_4_Board
  proto2 = Adafruit_PermaProto_1_4_Board
  VALVE1 = Plastic Solenoid Valve
  RE1 = Rotary Encoder [package=THT]
  5v = DC Power [voltage=5]  # not connected
  12v = DC Power [voltage=5]  # not connected
  U3 = SWITCH_SPDT [package=kps-1290]

nets:
  N1: Raspberry_Pi1.3v3, proto2.connectorW15
  N2: Raspberry_Pi1.GPIO4, proto1.connectorE15
  N3: Raspberry_Pi1.GND, proto1.connectorX5, proto2.connectorX15
  N4: Raspberry_Pi1.GPIO17, proto1.connectorE14
  N5: Raspberry_Pi1.GPIO24, proto1.connectorE12
  N6: Raspberry_Pi1.GPIO23, proto1.connectorE13
  N7: Raspberry_Pi1.5V, proto1.connectorW5
  N8: U1.T1, proto2.connectorW13
  N9: U1.T2, proto2.connectorE14
  N10: U1.+, U3.O
  N11: U1.-, proto2.connectorX4
  N12: U2.T1, proto2.connectorW14
  N13: U2.T2, proto2.connectorE15
  N14: proto1.connectorB12, proto2.connectorD15
  N15: proto1.connectorC13, proto2.connectorD14
  N16: proto1.connectorC15, RE1.EncoderPinC
  N17: proto1.connectorW15, RE1.EncoderPinB
  N18: proto1.connectorX15, RE1.EncoderPinA
  N19: proto2.connectorW1, U3.S
  N20: proto2.connectorX1, VALVE1.no_name_yet#2
  N21: VALVE1.no_name_yet#1, U3.P
